# Fritzing sketch completedclockwithlabels2 (saved by Fritzing 0.9.3b)
circuit board: 10cm x 10cm
breadboards: 8

parts:
  Part1 = Arduino Uno (Rev3)  # not connected
  TPIC2 = TPIC6B595
  TPIC3 = TPIC6B595
  TPIC4 = TPIC6B595
  C1 = Ceramic Capacitor [capacitance=0.1nF voltage=50V package="100 mil [THT, multilayer]"]
  IV-9 = TPIC6B595
  R9 = Resistor [tolerance=±5% resistance=100 package=THT]
  R10 = Resistor [tolerance=±5% resistance=100 package=THT]
  R11 = Resistor [tolerance=±5% resistance=100 package=THT]
  R12 = Resistor [tolerance=±5% resistance=100 package=THT]
  R13 = Resistor [tolerance=±5% resistance=100 package=THT]
  R14 = Resistor [tolerance=±5% resistance=100 package=THT]
  R15 = Resistor [tolerance=±5% resistance=100 package=THT]
  R16 = Resistor [tolerance=±5% resistance=100 package=THT]
  IV-9_2 = TPIC6B595
  R17 = Resistor [tolerance=±5% resistance=100 package=THT]
  R18 = Resistor [tolerance=±5% resistance=100 package=THT]
  R19 = Resistor [tolerance=±5% resistance=100 package=THT]
  R20 = Resistor [tolerance=±5% resistance=100 package=THT]
  R21 = Resistor [tolerance=±5% resistance=100 package=THT]
  R22 = Resistor [tolerance=±5% resistance=100 package=THT]
  R23 = Resistor [tolerance=±5% resistance=100 package=THT]
  R24 = Resistor [tolerance=±5% resistance=100 package=THT]
  TPIC1 = TPIC6B595
  IV-9_3 = TPIC6B595
  IV-9_4 = TPIC6B595
  R25 = Resistor [tolerance=±5% resistance=100 package=THT]
  R26 = Resistor [tolerance=±5% resistance=100 package=THT]
  R27 = Resistor [tolerance=±5% resistance=100 package=THT]
  R28 = Resistor [tolerance=±5% resistance=100 package=THT]
  R29 = Resistor [tolerance=±5% resistance=100 package=THT]
  R30 = Resistor [tolerance=±5% resistance=100 package=THT]
  R31 = Resistor [tolerance=±5% resistance=100 package=THT]
  R32 = Resistor [tolerance=±5% resistance=100 package=THT]
  R33 = Resistor [tolerance=±5% resistance=100 package=THT]
  R34 = Resistor [tolerance=±5% resistance=100 package=THT]
  R35 = Resistor [tolerance=±5% resistance=100 package=THT]
  R36 = Resistor [tolerance=±5% resistance=100 package=THT]
  R37 = Resistor [tolerance=±5% resistance=100 package=THT]
  R38 = Resistor [tolerance=±5% resistance=100 package=THT]
  R39 = Resistor [tolerance=±5% resistance=100 package=THT]
  R40 = Resistor [tolerance=±5% resistance=100 package=THT]
  R44 = Resistor [tolerance=±5% resistance=10k package=THT]
  DHT2 = DHT11 Humitidy and Temperature Sensor  # not connected
  B3 = Pushbutton [package="[THT]"]
  B1 = Pushbutton [package="[THT]"]
  B2 = Pushbutton [package="[THT]"]
  R45 = Resistor [tolerance=±5% resistance=10k package=THT]
  R46 = Resistor [tolerance=±5% resistance=10k package=THT]
  R47 = Resistor [tolerance=±5% resistance=10k package=THT]
  GRD_B3 = female pin header, 2 pins [form="♀ (female)"]
  B3_NA = female pin header, 2 pins [form="♀ (female)"]
  NA_B2 = female pin header, 2 pins [form="♀ (female)"]
  RCK_SRCK = female pin header, 2 pins [form="♀ (female)"]
  A1_5V = female pin header, 2 pins [form="♀ (female)"]

nets (from the pcb view):
  N1: TPIC2.SER_IN, TPIC1.SER_OUT
  N2: TPIC2.DRAIN0, R9.Pin_1
  N3: TPIC2.DRAIN1, R11.Pin_1
  N4: TPIC2.DRAIN2, R12.Pin_1
  N5: TPIC2.DRAIN3, R10.Pin_1
  VCC: TPIC2.SRCLR, TPIC2.VCC, TPIC3.SRCLR, TPIC3.VCC, TPIC4.SRCLR, TPIC4.VCC, C1.1, IV-9.NC, IV-9_2.NC, TPIC1.SRCLR, TPIC1.VCC, IV-9_3.NC, IV-9_4.NC, B3.Pin_1, B3.Pin_2, B1.Pin_1, B1.Pin_2, B2.Pin_1, B2.Pin_2, R46.Pin_1, A1_5V.pin2
  GND: TPIC2.G, TPIC2.GND, TPIC3.G, TPIC3.GND, TPIC4.G, TPIC4.GND, C1.0, TPIC1.G, TPIC1.GND, R44.Pin_1, R45.Pin_0, R46.Pin_0, R47.Pin_0, GRD_B3.pin1
  N6: TPIC2.RCK, TPIC3.RCK, TPIC4.RCK, TPIC1.RCK, RCK_SRCK.pin1
  N7: TPIC2.SRCK, TPIC3.SRCK, TPIC4.SRCK, TPIC1.SRCK, RCK_SRCK.pin2
  N8: TPIC2.DRAIN4, R16.Pin_1
  N9: TPIC2.DRAIN5, R15.Pin_1
  N10: TPIC2.DRAIN6, R14.Pin_1
  N11: TPIC2.DRAIN7, R13.Pin_1
  N12: TPIC2.SER_OUT, TPIC3.SER_IN
  N13: TPIC3.DRAIN0, R28.Pin_1
  N14: TPIC3.DRAIN1, R27.Pin_1
  N15: TPIC3.DRAIN2, R26.Pin_1
  N16: TPIC3.DRAIN3, R25.Pin_1
  N17: TPIC3.DRAIN4, R32.Pin_1
  N18: TPIC3.DRAIN5, R31.Pin_1
  N19: TPIC3.DRAIN6, R29.Pin_1
  N20: TPIC3.DRAIN7, R30.Pin_1
  N21: TPIC3.SER_OUT, TPIC4.SER_IN
  N22: TPIC4.DRAIN0, R35.Pin_1
  N23: TPIC4.DRAIN1, R36.Pin_1
  N24: TPIC4.DRAIN2, R34.Pin_1
  N25: TPIC4.DRAIN3, R33.Pin_1
  N26: TPIC4.DRAIN4, R40.Pin_1
  N27: TPIC4.DRAIN5, R39.Pin_1
  N28: TPIC4.DRAIN6, R38.Pin_1
  N29: TPIC4.DRAIN7, R37.Pin_1
  N30: TPIC4.SER_OUT, R44.Pin_0
  N31: IV-9.SER_IN, R9.Pin_0
  N32: IV-9.DRAIN1, R10.Pin_0
  N33: IV-9.DRAIN3, R11.Pin_0
  N34: IV-9.G, R12.Pin_0
  N35: IV-9.SRCK, R14.Pin_0
  N36: IV-9.DRAIN5, R13.Pin_0
  N37: IV-9.DRAIN7, R15.Pin_0
  N38: IV-9.GND, R16.Pin_0
  N39: IV-9_2.SER_IN, R20.Pin_0
  N40: IV-9_2.DRAIN1, R19.Pin_0
  N41: IV-9_2.DRAIN3, R17.Pin_0
  N42: IV-9_2.G, R18.Pin_0
  N43: IV-9_2.SRCK, R21.Pin_0
  N44: IV-9_2.DRAIN5, R22.Pin_0
  N45: IV-9_2.DRAIN7, R23.Pin_0
  N46: IV-9_2.GND, R24.Pin_0
  N47: R17.Pin_1, TPIC1.DRAIN3
  N48: R18.Pin_1, TPIC1.DRAIN2
  N49: R19.Pin_1, TPIC1.DRAIN0
  N50: R20.Pin_1, TPIC1.DRAIN1
  N51: R21.Pin_1, TPIC1.DRAIN7
  N52: R22.Pin_1, TPIC1.DRAIN6
  N53: R23.Pin_1, TPIC1.DRAIN5
  N54: R24.Pin_1, TPIC1.DRAIN4
  N55: TPIC1.SER_IN, A1_5V.pin1
  N56: IV-9_3.SER_IN, R28.Pin_0
  N57: IV-9_3.DRAIN1, R25.Pin_0
  N58: IV-9_3.DRAIN3, R26.Pin_0
  N59: IV-9_3.G, R27.Pin_0
  N60: IV-9_3.SRCK, R29.Pin_0
  N61: IV-9_3.DRAIN5, R30.Pin_0
  N62: IV-9_3.DRAIN7, R31.Pin_0
  N63: IV-9_3.GND, R32.Pin_0
  N64: IV-9_4.SER_IN, R35.Pin_0
  N65: IV-9_4.DRAIN1, R33.Pin_0
  N66: IV-9_4.DRAIN3, R36.Pin_0
  N67: IV-9_4.G, R34.Pin_0
  N68: IV-9_4.SRCK, R37.Pin_0
  N69: IV-9_4.DRAIN5, R38.Pin_0
  N70: IV-9_4.DRAIN7, R39.Pin_0
  N71: IV-9_4.GND, R40.Pin_0
  N72: B3.Pin_3, B3.Pin_4, R47.Pin_1, B3_NA.pin1
  N73: B1.Pin_3, B1.Pin_4, GRD_B3.pin2
  N74: B2.Pin_3, B2.Pin_4, R45.Pin_1, NA_B2.pin2

notes:
  Babybird Numitron Clock
  it took 12 years to make

custom parts:
  TPIC6B595: 8-bit high-power parallel-load shift register
  TPIC6B595: 8-bit high-power parallel-load shift register
  DHT11 Humitidy and Temperature Sensor: DHT11 Humidity and Temperature Sensor
